# Fritzing sketch Sketch (saved by Fritzing 0.9.2b)
breadboards: 1

parts:
  Raspberry_Pi1 = Raspberry Pi 2
  IC1 = MCP3008 8-channel 10-bit ADC [part_number=MCP3008]
  U1 = TMP36 [package=to-92-kit]

nets:
  N1: Raspberry_Pi1.GPIO10, IC1.no_name_yet#11
  N2: Raspberry_Pi1.GPIO9, IC1.no_name_yet#12
  N3: Raspberry_Pi1.GPIO11, IC1.no_name_yet#13
  N4: Raspberry_Pi1.GND, IC1.no_name_yet#9, IC1.no_name_yet#14
  N5: Raspberry_Pi1.GPIO8, IC1.no_name_yet#10
  N6: Raspberry_Pi1.5V, IC1.no_name_yet#16
  N7: IC1.no_name_yet#1, U1.VOUT
